# Fritzing sketch circuit (saved by Fritzing 0.9.3b)
breadboards: 1

parts:
  Arduino_UNO = Arduino Uno (Rev3)
  IN1 = 3.5mm Audio Jack [package=audio-jack-3.5mm-smd]
  IN2 = 3.5mm Audio Jack [package=audio-jack-3.5mm-smd]
  OUT = 3.5mm Audio Jack [package=audio-jack-3.5mm-smd]
  S1 = SWITCH-DPDT [package=eg2211]
  R1 = Resistor [tolerance=±5% resistance=1k package=THT]
  R2 = Resistor [tolerance=±5% resistance=1k package=THT]
  C1 = Ceramic Capacitor [capacitance=47µF package="100 mil [THT, multilayer]"]
  C2 = Ceramic Capacitor [capacitance=47µF package="100 mil [THT, multilayer]"]
  R3 = Resistor [tolerance=±5% resistance=10k package=THT]
  R4 = Resistor [tolerance=±5% resistance=10k package=THT]
  R5 = Resistor [tolerance=±5% resistance=10k package=THT]
  R6 = Resistor [tolerance=±5% resistance=10k package=THT]
  V1 = DC Power [voltage=5]
  NEOPIXEL1 = Neopixel Strip -- White (30/m)
  S2 = Taiway 100-SP-X-T1 SPDT Miniature Toggle Switch [part_number=SPST package=THT]

nets:
  GND: Arduino_UNO.GND, IN1.SLEEVE, IN2.SLEEVE, OUT.SLEEVE, R3.Pin_1, R5.Pin_0, V1.V-, NEOPIXEL1.GND
  N1: Arduino_UNO.A4/SDA, C1.0, R5.Pin_1, R6.Pin_1
  N2: Arduino_UNO.A5/SCL, C2.0, R3.Pin_0, R4.Pin_1
  N3: Arduino_UNO.D6_PWM, NEOPIXEL1.Din
  N4: Arduino_UNO.5V, R4.Pin_0, R6.Pin_0
  VIN: Arduino_UNO.VIN, NEOPIXEL1.+5V, S2.COM
  N5: IN1.RIGHT, S1.1
  N6: IN1.LEFT, S1.4
  N7: IN2.RIGHT, S1.3
  N8: IN2.LEFT, S1.6
  N9: OUT.RIGHT, S1.2, R1.Pin_0
  N10: OUT.LEFT, S1.5, R2.Pin_0
  N11: R1.Pin_1, C1.1
  N12: R2.Pin_1, C2.1
  N13: V1.V+, S2.L1

custom parts:
  Neopixel Strip -- White (30/m): These NeoPixel strips have 30 digitally-addressable pixel LEDs per meter and are very affordable and are only 12.5 mm wide, 10 mm if you remove the strip from the casing.
